# Fritzing sketch TFG-ECG (saved by Fritzing 0.9.3b)
breadboards: 1

parts:
  U1 = ESP32-38PinWide [part_number=ESP32-38PinWide]
  IC2 = AD8232 HeartRate Monitor [part_number=SEN-12650 chip_label=IC package="DIP (Dual Inline) [THT]"]
  Part1 = Adafruit ADS1115 16Bit I2C ADC [part_number="Adafruit #1085"]

nets:
  3.3V: U1.3.3, IC2.3.3v, Part1.VDD
  GND: U1.GND, IC2.GND, Part1.GND
  N1: U1.GPIO21, Part1.SDA
  N2: U1.GPIO22, Part1.SCL

custom parts:
  ESP32-38PinWide: Generic 38-Pin ESP32 with wide format (only access to one side of pins on a breadboard) based on Stephen Lilley's HiLetgo ESP-WROOM-32 ESP32 ESP-32S Development Board.
  AD8232 HeartRate Monitor: A DIP stand-in part for whatever IC you want. With 10 pins on a 600mil dual inline package (DIP) footprint.
  Adafruit ADS1115 16Bit I2C ADC: For microcontrollers without an analog-to-digital converter or when you want a higher-precision ADC, the ADS1115 provides 16-bit precision at 860 samples/second over I2C. The chip can be configured as 4 single-ended input channels, or two differential channels. As a nice bonus, it even includes a programmable gain amplifier, up to x16, to help boost up smaller single/differential signals to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
